# Fritzing sketch low_pass_filter_v1 (saved by Fritzing 0.9.3b)
stripboards: 1

parts:
  C1 = Ceramic Capacitor [capacitance=0.22nF voltage=35V package="0603 [SMD, multilayer]"]
  R1 = Resistor [tolerance=±5% power=0.25 resistance=270 package=THT]
  R2 = Resistor [tolerance=±5% power=0.25 resistance=150 package=THT]
  C3 = Ceramic Capacitor [capacitance=0.22nF voltage=35V package="0603 [SMD, multilayer]"]
  R4 = Resistor [tolerance=±5% power=0.25 resistance=150 package=THT]
  C4 = Electrolytic Capacitor [capacitance=1µF voltage=35V package="100 mil [THT, electrolytic]"]
  R5 = Resistor [tolerance=±5% power=0.25 resistance=270 package=THT]
  Part1 = TRRS 3.5mm Jack Breakout
  C2 = Electrolytic Capacitor [capacitance=1µF voltage=35V package="100 mil [THT, electrolytic]"]
  Raspberry_Pi1 = Raspberry Pi Zero

nets:
  N1: C1.0, R1.Pin_0, R2.Pin_0, C4.+
  N2: C1.1, R2.Pin_1, C3.1, R4.Pin_1
  N3: R1.Pin_1, Raspberry_Pi1.GIPO13
  N4: C3.0, R4.Pin_0, R5.Pin_0, C2.+
  N5: C4.-, Part1.TIP
  N6: R5.Pin_1, Raspberry_Pi1.GIPO12
  N7: Part1.SLEEVE, C2.-
  N8: Part1.RING2, Raspberry_Pi1.GND
  N9: Part1.RING1, Raspberry_Pi1.TV_signal

custom parts:
  Raspberry Pi Zero: The Raspberry Pi Zero is the latest single board computer to be released by the Raspberry Pi Foundation. It is the entry level model Raspberry Pi perfect for hobbyists, makers and industrial engineers looking to create solutions where small size and low power consumption are important. This is especially relevant for applications in the wearables space as well as up and coming applications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
